// Logisim project Lab2.circ as structural Verilog: 7 circuits, main circuit main
module main (
);


  // Notes on the sheet:
  //   Lab 2
  //   Alejandro Sanabria Portala
  //   Matthew Paquette
endmodule

module mux_2x1 (
  input  S,
  input  A,
  input  B,
  output C
);

  wire and_1_out, and_2_out, not_1_out;

  not not_1 (not_1_out, S);
  and and_1 (and_1_out, not_1_out, A);
  and and_2 (and_2_out, S, B);
  or or_1 (C, and_1_out, and_2_out);
endmodule

module mux_4x1 (
  input  S1,
  input  S0,
  input  A,
  input  B,
  input  C,
  input  D,
  output E
);

  wire mux_2x1_1_c, mux_2x1_2_c;

  mux_2x1 mux_2x1_1 (.S(S0), .A(A), .B(B), .C(mux_2x1_1_c));
  mux_2x1 mux_2x1_2 (.S(S0), .A(C), .B(D), .C(mux_2x1_2_c));
  mux_2x1 mux_2x1_3 (.S(S1), .A(mux_2x1_1_c), .B(mux_2x1_2_c), .C(E));
endmodule

module part3a (
  input  B1,
  input  B0,
  output A,
  output B,
  output C,
  output D,
  output E,
  output F,
  output G
);

  wire not_1_out, not_2_out, not_3_out;

  not not_1 (not_1_out, B1);
  and and_1 (A, not_1_out, B0);
  and and_2 (C, B1, not_2_out);
  not not_2 (not_2_out, B0);
  not not_3 (not_3_out, B1);
  and and_3 (D, not_3_out, B0);
  or or_1 (F, B0, B1);
  not not_4 (G, B1);

  assign B = 1'b0;
  assign E = B0;

  // Notes on the sheet:
  //   part3a
endmodule

module seven_segment (
  input  B0,
  input  B1,
  input  B2,
  input  B3,
  output [7:0] display_out
);

  wire [7:0] mux_4x1_8bit_1_e, mux_4x1_8bit_2_e, mux_4x1_8bit_3_e, mux_4x1_8bit_4_e;

  mux_4x1_8bit mux_4x1_8bit_1 (.S1(B1), .S0(B0), .A(8'hc0), .B(8'hf9), .C(8'ha4), .D(8'hb0), .E(mux_4x1_8bit_1_e));
  mux_4x1_8bit mux_4x1_8bit_2 (.S1(B1), .S0(B0), .A(8'h99), .B(8'h92), .C(8'h82), .D(8'hf8), .E(mux_4x1_8bit_2_e));
  mux_4x1_8bit mux_4x1_8bit_3 (.S1(B1), .S0(B0), .A(8'h80), .B(8'h90), .C(8'h88), .D(8'h83), .E(mux_4x1_8bit_3_e));
  mux_4x1_8bit mux_4x1_8bit_4 (.S1(B1), .S0(B0), .A(8'hc6), .B(8'ha1), .C(8'h86), .D(8'h8e), .E(mux_4x1_8bit_4_e));
  mux_4x1_8bit mux_4x1_8bit_5 (
    .S1(B3), .S0(B2), .A(mux_4x1_8bit_1_e), .B(mux_4x1_8bit_2_e), .C(mux_4x1_8bit_3_e), .D(mux_4x1_8bit_4_e),
    .E(display_out));
endmodule

module mux_4x1_8bit (
  input  S1,
  input  S0,
  input  [7:0] A,
  input  [7:0] B,
  input  [7:0] C,
  input  [7:0] D,
  output [7:0] E
);

  mux_4x1 mux_0 (.S1(S1), .S0(S0), .A(A[0]), .B(B[0]), .C(C[0]), .D(D[0]), .E(E[0]));
  mux_4x1 mux_1 (.S1(S1), .S0(S0), .A(A[1]), .B(B[1]), .C(C[1]), .D(D[1]), .E(E[1]));
  mux_4x1 mux_2 (.S1(S1), .S0(S0), .A(A[2]), .B(B[2]), .C(C[2]), .D(D[2]), .E(E[2]));
  mux_4x1 mux_3 (.S1(S1), .S0(S0), .A(A[3]), .B(B[3]), .C(C[3]), .D(D[3]), .E(E[3]));
  mux_4x1 mux_4 (.S1(S1), .S0(S0), .A(A[4]), .B(B[4]), .C(C[4]), .D(D[4]), .E(E[4]));
  mux_4x1 mux_5 (.S1(S1), .S0(S0), .A(A[5]), .B(B[5]), .C(C[5]), .D(D[5]), .E(E[5]));
  mux_4x1 mux_6 (.S1(S1), .S0(S0), .A(A[6]), .B(B[6]), .C(C[6]), .D(D[6]), .E(E[6]));
  mux_4x1 mux_7 (.S1(S1), .S0(S0), .A(A[7]), .B(B[7]), .C(C[7]), .D(D[7]), .E(E[7]));
endmodule

module part4 (
  input  S1,
  input  S0
);
endmodule
